// Logisim project week 4 cpu - alu starter.circ as structural Verilog: 1 circuit, main circuit ALU
module ALU (
  input  [7:0] A,
  input  [7:0] B,
  input  [1:0] Operation,
  output [7:0] ALU_Out
);

  wire [7:0] adder_1_out, and_1_out, shifter_1_out, subtractor_1_out;

  Adder adder_1 (.a(A), .b(B), .out(adder_1_out));  // open: cin, cout
  assign and_1_out = A & B;  // AND_Gate and_1, 8 bits wide
  Subtractor subtractor_1 (.a(A), .b(8'h1), .out(subtractor_1_out));  // open: bin, bout
  Shifter shifter_1 (.in(A), .\dist (3'b001), .out(shifter_1_out));
  Multiplexer #(.select(2), .width(8)) multiplexer_1 (
    .in0(adder_1_out), .in1(and_1_out), .in2(subtractor_1_out), .in3(shifter_1_out), .out(ALU_Out),
    .sel(Operation));  // open: en
endmodule
